// Logisim project 67.circ as structural Verilog: 1 circuit, main circuit main
module main (
);

  wire and_1_out, and_2_out, and_3_out, and_4_out, and_5_out, and_6_out, and_7_out, and_8_out, and_9_out,
       and_10_out, and_11_out, and_12_out, and_13_out, and_14_out, and_15_out, and_16_out, and_17_out,
       and_18_out, and_19_out, and_20_out, and_21_out, and_22_out, and_23_out, and_24_out, and_25_out,
       and_26_out, and_27_out, and_28_out, clock_1_out, nand_1_out, nand_2_out, nand_3_out, nand_4_out,
       nand_5_out, nand_6_out, nand_7_out, nand_8_out, nand_9_out, nand_10_out, nand_11_out, nand_12_out,
       nand_13_out, nand_14_out, nand_15_out, nand_16_out, nand_17_out, nand_18_out, nand_19_out,
       nand_20_out, nand_21_out, nand_22_out, nand_23_out, nand_24_out, nand_25_out, nand_26_out,
       nand_27_out, nand_28_out, nand_29_out, nand_30_out, nand_31_out, nand_32_out, nand_33_out,
       nand_34_out, nand_35_out, nand_36_out, not_1_out, not_2_out, not_3_out, not_4_out, not_5_out,
       not_6_out, not_7_out, not_8_out, not_9_out, not_10_out, not_11_out, not_12_out, or_1_out, or_2_out,
       or_3_out, or_4_out, or_5_out, or_6_out, or_7_out, or_8_out;

  nand nand_1 (nand_1_out, 1'b1, 1'b1);
  nand nand_2 (nand_2_out, 1'b1, nand_1_out);
  nand nand_3 (nand_3_out, nand_1_out, 1'b1);
  nand nand_4 (nand_4_out, nand_2_out, nand_3_out);
  nand nand_5 (nand_5_out, 1'b1, 1'b1);
  nand nand_6 (nand_6_out, nand_4_out, 1'b0);
  nand nand_7 (nand_7_out, 1'b1, nand_5_out);
  nand nand_8 (nand_8_out, nand_5_out, 1'b1);
  nand nand_9 (nand_9_out, 1'b1, 1'b1);
  nand nand_10 (nand_10_out, nand_4_out, nand_6_out);
  nand nand_11 (nand_11_out, nand_6_out, 1'b0);
  nand nand_12 (nand_12_out, nand_7_out, nand_8_out);
  nand nand_13 (nand_13_out, nand_10_out, nand_11_out);
  nand nand_14 (nand_14_out, nand_6_out, nand_1_out);
  nand nand_15 (nand_15_out, 1'b1, nand_9_out);
  nand nand_16 (nand_16_out, nand_9_out, 1'b1);
  LED led_1 (.in(nand_13_out));
  nand nand_17 (nand_17_out, nand_12_out, nand_14_out);
  nand nand_18 (nand_18_out, nand_12_out, nand_17_out);
  nand nand_19 (nand_19_out, nand_17_out, nand_14_out);
  nand nand_20 (nand_20_out, nand_15_out, nand_16_out);
  nand nand_21 (nand_21_out, nand_17_out, nand_5_out);
  nand nand_22 (nand_22_out, nand_18_out, nand_19_out);
  nand nand_23 (nand_23_out, nand_20_out, nand_21_out);
  LED led_2 (.in(nand_22_out));
  nand nand_24 (nand_24_out, nand_20_out, nand_23_out);
  nand nand_25 (nand_25_out, nand_23_out, nand_21_out);
  nand nand_26 (nand_26_out, 1'b1, 1'b1);
  nand nand_27 (nand_27_out, nand_23_out, nand_9_out);
  nand nand_28 (nand_28_out, nand_24_out, nand_25_out);
  nand nand_29 (nand_29_out, 1'b1, nand_26_out);
  nand nand_30 (nand_30_out, nand_26_out, 1'b1);
  LED led_3 (.in(nand_28_out));
  nand nand_31 (nand_31_out, nand_29_out, nand_30_out);
  Clock clock_1 (.out(clock_1_out));
  nand nand_32 (nand_32_out, nand_31_out, nand_27_out);
  nand nand_33 (nand_33_out, nand_31_out, nand_32_out);
  nand nand_34 (nand_34_out, nand_32_out, nand_27_out);
  not not_1 (not_1_out, 1'b0);
  not not_2 (not_2_out, clock_1_out);
  not not_3 (not_3_out, clock_1_out);
  nand nand_35 (nand_35_out, nand_33_out, nand_34_out);
  nand nand_36 (nand_36_out, nand_32_out, nand_26_out);
  and and_1 (and_1_out, 1'b0, clock_1_out);
  and and_2 (and_2_out, clock_1_out, clock_1_out);
  and and_3 (and_3_out, 1'b0, clock_1_out);
  LED led_4 (.in(nand_35_out));
  LED led_5 (.in(nand_36_out));
  or or_1 (or_1_out, and_1_out, and_2_out, and_3_out);
  and and_4 (and_4_out, not_1_out, not_2_out, clock_1_out);
  and and_5 (and_5_out, not_1_out, clock_1_out, not_3_out);
  and and_6 (and_6_out, 1'b0, not_2_out, not_3_out);
  and and_7 (and_7_out, 1'b0, clock_1_out, clock_1_out);
  not not_4 (not_4_out, 1'b0);
  not not_5 (not_5_out, 1'b1);
  not not_6 (not_6_out, or_1_out);
  or or_2 (or_2_out, and_4_out, and_5_out, and_6_out, and_7_out);
  and and_8 (and_8_out, 1'b0, 1'b1);
  and and_9 (and_9_out, 1'b1, or_1_out);
  and and_10 (and_10_out, 1'b0, or_1_out);
  LED led_6 (.in(or_2_out));
  or or_3 (or_3_out, and_8_out, and_9_out, and_10_out);
  and and_11 (and_11_out, not_4_out, not_5_out, or_1_out);
  and and_12 (and_12_out, not_4_out, 1'b1, not_6_out);
  and and_13 (and_13_out, 1'b0, not_5_out, not_6_out);
  and and_14 (and_14_out, 1'b0, 1'b1, or_1_out);
  not not_7 (not_7_out, 1'b0);
  not not_8 (not_8_out, 1'b1);
  not not_9 (not_9_out, or_3_out);
  and and_15 (and_15_out, 1'b0, 1'b1);
  and and_16 (and_16_out, 1'b1, or_3_out);
  and and_17 (and_17_out, 1'b0, or_3_out);
  or or_4 (or_4_out, and_11_out, and_12_out, and_13_out, and_14_out);
  LED led_7 (.in(or_4_out));
  or or_5 (or_5_out, and_15_out, and_16_out, and_17_out);
  and and_18 (and_18_out, not_7_out, not_8_out, or_3_out);
  and and_19 (and_19_out, not_7_out, 1'b1, not_9_out);
  and and_20 (and_20_out, 1'b0, not_8_out, not_9_out);
  and and_21 (and_21_out, 1'b0, 1'b1, or_3_out);
  not not_10 (not_10_out, 1'b1);
  not not_11 (not_11_out, 1'b0);
  not not_12 (not_12_out, or_5_out);
  and and_22 (and_22_out, 1'b1, 1'b0);
  and and_23 (and_23_out, 1'b0, or_5_out);
  and and_24 (and_24_out, 1'b1, or_5_out);
  or or_6 (or_6_out, and_18_out, and_19_out, and_20_out, and_21_out);
  LED led_8 (.in(or_6_out));
  and and_25 (and_25_out, not_10_out, not_11_out, or_5_out);
  and and_26 (and_26_out, not_10_out, 1'b0, not_12_out);
  and and_27 (and_27_out, 1'b1, not_11_out, not_12_out);
  and and_28 (and_28_out, 1'b1, 1'b0, or_5_out);
  or or_7 (or_7_out, and_22_out, and_23_out, and_24_out);
  LED led_9 (.in(or_7_out));
  or or_8 (or_8_out, and_25_out, and_26_out, and_27_out, and_28_out);
  LED led_10 (.in(or_8_out));
endmodule
